# Fritzing sketch arduino-piezos-2 (saved by Fritzing 0.9.3b)
breadboards: 1

parts:
  R1 = Resistor [tolerance=±5% resistance=1M package=THT]
  R2 = Resistor [tolerance=±5% resistance=1M package=THT]
  D5 = Zener Diode 2 [part_number=1N4732A package="300 mil [THT]"]
  D6 = Zener Diode 2 [part_number=1N4732A package="300 mil [THT]"]
  U3 = 3.5mm Mono Audio Jack [package=audio-jack]
  U4 = 3.5mm Mono Audio Jack [package=audio-jack]
  J3 = Screw terminal - 5 pins - 3.81mm pin spacing [package=THT]
  R3 = Resistor [tolerance=±5% resistance=1M package=THT]
  R4 = Resistor [tolerance=±5% resistance=1M package=THT]
  D7 = Zener Diode 2 [part_number=1N4732A package="300 mil [THT]"]
  D8 = Zener Diode 2 [part_number=1N4732A package="300 mil [THT]"]
  U5 = 3.5mm Mono Audio Jack [package=audio-jack]
  U6 = 3.5mm Mono Audio Jack [package=audio-jack]

nets:
  N1: R1.Pin_0, R2.Pin_0, D5.anode, D6.anode, U3.SLEEVE, U4.SLEEVE, J3.pin1, R3.Pin_0, R4.Pin_0, D7.anode, D8.anode, U5.SLEEVE, U6.SLEEVE
  N2: R1.Pin_1, D6.cathode, U3.SIGNAL, J3.pin2
  N3: R2.Pin_1, D5.cathode, U4.SIGNAL, J3.pin3
  N4: J3.pin4, R3.Pin_1, D7.cathode, U6.SIGNAL
  N5: J3.pin5, R4.Pin_1, D8.cathode, U5.SIGNAL

notes:
  Gnd, A0, A1, A2, A3
  GND
  A0
  A1

custom parts:
  Zener Diode 2: A standard zener diode with corrected terminal points (YL)
  3.5mm Mono Audio Jack: Simple 3.5mm MONO PCB mount audio jack. Manufacturer: LUMBERG Manufacturer Part No: 1503 12 Order Code: 1340604
  Screw terminal - 5 pins - 3.81mm pin spacing: Screw terminal with 5 pins. 3.81mm pin spacing
