# Fritzing sketch arduino-piezos-4 (saved by Fritzing 0.9.3b)
breadboards: 1

parts:
  Part1 = Arduino Uno (Rev3)
  U1 = 3.5mm Audio Jack [package=audio-jack]
  R1 = Resistor [tolerance=±5% resistance=1M package=THT]
  D1 = Zener Diode [part_number=1N4732A breakdown_voltage=4.7V package="300 mil [THT]"]
  U2 = 3.5mm Audio Jack [package=audio-jack]
  R2 = Resistor [tolerance=±5% resistance=1M package=THT]
  D2 = Zener Diode [part_number=1N4732A breakdown_voltage=4.7V package="300 mil [THT]"]
  U3 = 3.5mm Audio Jack [package=audio-jack]
  R3 = Resistor [tolerance=±5% resistance=1M package=THT]
  D3 = Zener Diode [part_number=1N4732A breakdown_voltage=4.7V package="300 mil [THT]"]
  U4 = 3.5mm Audio Jack [package=audio-jack]
  R4 = Resistor [tolerance=±5% resistance=1M package=THT]
  D4 = Zener Diode [part_number=1N4732A breakdown_voltage=4.7V package="300 mil [THT]"]

nets:
  N1: Part1.A0, U1.RIGHT, R1.Pin_1, D4.cathode
  N2: Part1.A1, U2.RIGHT, R2.Pin_1, D3.cathode
  N3: Part1.A2, D2.cathode, U3.RIGHT, R3.Pin_1
  N4: Part1.A3, D1.cathode, U4.RIGHT, R4.Pin_1
  N5: Part1.GND, U1.SLEEVE, R1.Pin_0, D1.anode, U2.SLEEVE, R2.Pin_0, D2.anode, U3.SLEEVE, R3.Pin_0, D3.anode, U4.SLEEVE, R4.Pin_0, D4.anode
