# Fritzing sketch arduino-piezos (saved by Fritzing 0.9.3b)
circuit board: 6.2cm x 4.1cm
breadboards: 1

parts:
  R0 = Resistor [tolerance=±5% resistance=1M package=THT]
  R1 = Resistor [tolerance=±5% resistance=1M package=THT]
  D1 = Zener Diode 2 [part_number=1N4732A package="300 mil [THT]"]
  D0 = Zener Diode 2 [part_number=1N4732A package="300 mil [THT]"]
  J3 = Screw terminal - 5 pins - 3.81mm pin spacing [package=THT]
  R2 = Resistor [tolerance=±5% resistance=1M package=THT]
  R3 = Resistor [tolerance=±5% resistance=1M package=THT]
  D2 = Zener Diode 2 [part_number=1N4732A package="300 mil [THT]"]
  D3 = Zener Diode 2 [part_number=1N4732A package="300 mil [THT]"]
  J3_2 = 3.5mm Mono Audio Jack [package=audio-jack]
  J2 = 3.5mm Mono Audio Jack [package=audio-jack]
  J0 = 3.5mm Mono Audio Jack [package=audio-jack]
  J1 = 3.5mm Mono Audio Jack [package=audio-jack]

nets:
  N1: R0.Pin_0, R1.Pin_0, D1.anode, D0.anode, J3.pin1, R2.Pin_0, R3.Pin_0, D2.anode, D3.anode, J3_2.SLEEVE, J2.SLEEVE, J0.SLEEVE, J1.SLEEVE
  N2: R0.Pin_1, D0.cathode, J3.pin2, J0.SIGNAL
  N3: R1.Pin_1, D1.cathode, J3.pin3, J1.SIGNAL
  N4: J3.pin4, R2.Pin_1, D2.cathode, J2.SIGNAL
  N5: J3.pin5, R3.Pin_1, D3.cathode, J3_2.SIGNAL

notes:
  Gnd, A0, A1, A2, A3
  GND
  A0
  A1
  A2
  A3
  Piezo to
  Arduino

custom parts:
  Zener Diode 2: A standard zener diode with corrected terminal points (YL)
  Screw terminal - 5 pins - 3.81mm pin spacing: Screw terminal with 5 pins. 3.81mm pin spacing
  3.5mm Mono Audio Jack: Simple 3.5mm MONO PCB mount audio jack. Manufacturer: LUMBERG Manufacturer Part No: 1503 12 Order Code: 1340604
