# Fritzing sketch arduino-piezos (saved by Fritzing 0.9.3b)
circuit board: 9.69966cm x 4.82455cm
breadboards: 1

parts:
  R0 = Resistor [tolerance=±5% resistance=1M package=THT]
  R1 = Resistor [tolerance=±5% resistance=1M package=THT]
  D1 = Zener Diode 2 [part_number=1N4732A package="300 mil [THT]"]
  D0 = Zener Diode 2 [part_number=1N4732A package="300 mil [THT]"]
  R2 = Resistor [tolerance=±5% resistance=1M package=THT]
  R3 = Resistor [tolerance=±5% resistance=1M package=THT]
  D2 = Zener Diode 2 [part_number=1N4732A package="300 mil [THT]"]
  D3 = Zener Diode 2 [part_number=1N4732A package="300 mil [THT]"]
  J4 = Screw terminal - 5 pins - 3.5mm pin spacing [package=THT]
  I2 = 6.35mm Mono Audio Jack Fixed [package=audio-jack]
  I1 = 6.35mm Mono Audio Jack Fixed [package=audio-jack]
  I0 = 6.35mm Mono Audio Jack Fixed [package=audio-jack]
  I3 = 6.35mm Mono Audio Jack Fixed [package=audio-jack]

nets:
  N1: R0.Pin_0, R1.Pin_0, D1.anode, D0.anode, R2.Pin_0, R3.Pin_0, D2.anode, D3.anode, J4.pin1, I2.SLEEVE, I1.SLEEVE, I0.SLEEVE, I3.SLEEVE
  N2: R0.Pin_1, D0.cathode, J4.pin2, I0.SIGNAL
  N3: R1.Pin_1, D1.cathode, J4.pin3, I1.SIGNAL
  N4: R2.Pin_1, D2.cathode, J4.pin4, I2.SIGNAL
  N5: R3.Pin_1, D3.cathode, J4.pin5, I3.SIGNAL

notes:
  Gnd, A0, A1, A2, A3
  GND
  A0
  A1
  A2
  A3
  Piezo to
  Arduino
  Fire Ancestor

custom parts:
  Zener Diode 2: A standard zener diode with corrected terminal points (YL)
  Screw terminal - 5 pins - 3.5mm pin spacing: Screw terminal with 5 pins. 3.5mm pin spacing
  6.35mm Mono Audio Jack Fixed: 6.35mm MONO PCB mount audio jack.
