# Fritzing sketch vfd-digipot (saved by Fritzing 0.9.3b)
circuit board: 4.29215cm x 2.82151cm
breadboards: 1

parts:
  MCP41X1 = IC, DIP package, 8 pins [chip_label=MCP41X1]
  VFD = screw terminal, 3 pins
  RPi = screw terminal, 5 pins

nets:
  N1: MCP41X1.pin1, RPi.pin4
  N2: MCP41X1.pin2, RPi.pin3
  N3: MCP41X1.pin3, RPi.pin2
  N4: MCP41X1.pin4, RPi.pin1
  N5: MCP41X1.pin5, VFD.pin3
  N6: MCP41X1.pin6, VFD.pin2
  N7: MCP41X1.pin7, VFD.pin1
  N8: MCP41X1.pin8, RPi.pin5

notes:
  CE0
  SCLK
  MOSI
  GND
  5V
  +10V
  AI
  COM
  Fire Ancestor
  VFD Digipot
